# Fritzing sketch motors (saved by Fritzing 0.9.3b)
breadboards: 1

parts:
  Part1 = Arduino Uno (Rev3)
  VCC1 = Battery block 9V
  M1 = DC Motor  # not connected
  M2 = DC Motor  # not connected

nets:
  N1: Part1.GND, VCC1.-
  N2: Part1.VIN, VCC1.+
